# Fritzing sketch Interphone Project one (saved by Fritzing 1.0.8)
breadboards: 1

parts:
  M1 = ESP32-S3-DevKitC-1-N8R8-v1 [part_number=ESP32-S3-DevKitC-1-N8R8-v1]
  R1 = Resistor [tolerance=±5% power=0.25W resistance=330 package=THT]
  LED1 = LED - 5mm [color="Red (633nm)" current=0.030A package="5 mm [THT]"]
  R2 = Resistor [tolerance=±5% power=0.25W resistance=330 package=THT]
  LED2 = LED - 5mm [color="Red (633nm)" current=0.030A package="5 mm [THT]"]
  D1 = Rectifier Diode [part_number=1N4001 package="300 mil [THT]"]
  R3 = Resistor [tolerance=±5% power=0.25W resistance=10k package=THT]
  R4 = Resistor [tolerance=±5% power=0.25W resistance=1k package=THT]
  S1 = Pushbutton [package="[THT]"]
  Part1 = KY-019 5V Relay Module [package="Breakout board"]
  J1 = Buzzer

nets:
  N1: M1.pin_1, M1.pin_2, D1.cathode, R3.Pin_0, Part1.Common
  N2: M1.pin_5, Part1.S
  N3: M1.pin_6, R2.Pin_0
  N4: M1.pin_12, R4.Pin_0
  N5: M1.pin_21, M1.pin_22, M1.pin_23, M1.pin_24, M1.pin_44, D1.anode, S1.Pin_1, S1.Pin_2, Part1.+, Part1.-, J1.pin1
  N6: M1.pin_27, R3.Pin_1, S1.Pin_3, S1.Pin_4
  N7: R1.Pin_0, Part1.NO
  N8: R1.Pin_1, LED1.cathode
  N9: LED1.anode, LED2.anode
  N10: R2.Pin_1, LED2.cathode

custom parts:
  ESP32-S3-DevKitC-1-N8R8-v1: ESP32-S3-DevKitC-1-N8R8-v1 This module is 44pins long (2x22) and 11 pins width.
  KY-019 5V Relay Module: KY-019 5V Relay module, used to control AC circuits.
  Buzzer: Fixed frequency buzzer
