# Fritzing sketch Interphone Project two (saved by Fritzing 1.0.8)
breadboards: 1

parts:
  M1 = ESP32-S3-DevKitC-1-N8R8-v1 [part_number=ESP32-S3-DevKitC-1-N8R8-v1]
  R1 = Resistor [tolerance=±5% power=0.25W resistance=330 package=THT]
  LED1 = LED - 5mm [color="Red (633nm)" current=0.030A package="5 mm [THT]"]
  R2 = Resistor [tolerance=±5% power=0.25W resistance=330 package=THT]
  LED2 = LED - 5mm [color="Red (633nm)" current=0.030A package="5 mm [THT]"]
  D1 = Rectifier Diode [part_number=1N4001 package="300 mil [THT]"]
  R3 = Resistor [tolerance=±5% power=0.25W resistance=10k package=THT]
  S1 = Pushbutton [package="[THT]"]
  R4 = Resistor [tolerance=±5% power=0.25W resistance=1k package=THT]
  Q1 = NPN-Transistor [package="TO92 [THT]"]
  J1 = Buzzer
  Part1 = KY-019 5V Relay Module [package="Breakout board"]

nets:
  N1: M1.pin_1, M1.pin_2, R3.Pin_0
  N2: M1.pin_5, Part1.S
  N3: M1.pin_6, R2.Pin_0
  N4: M1.pin_11, R4.Pin_0
  N5: M1.pin_21, D1.cathode, J1.pin1, Part1.+, Part1.Common
  N6: M1.pin_22, M1.pin_23, M1.pin_24, M1.pin_44, LED1.cathode, LED2.cathode, S1.Pin_1, S1.Pin_2, Q1.E, Part1.-
  N7: M1.pin_27, R3.Pin_1, S1.Pin_3, S1.Pin_4
  N8: R1.Pin_0, Part1.NO
  N9: R1.Pin_1, LED1.anode
  N10: R2.Pin_1, LED2.anode
  N11: D1.anode, Q1.C, J1.pin2
  N12: R4.Pin_1, Q1.B

custom parts:
  ESP32-S3-DevKitC-1-N8R8-v1: ESP32-S3-DevKitC-1-N8R8-v1 This module is 44pins long (2x22) and 11 pins width.
  Buzzer: Fixed frequency buzzer
  KY-019 5V Relay Module: KY-019 5V Relay module, used to control AC circuits.
